# Fritzing sketch watchdog-20151019-scheme (saved by Fritzing 0.9.2b)

parts:
  Arduino_Nano_V3_0 = Arduino Nano (Rev3.0)
  JP1 = Header 5x2 [package=2x5-ra]
  W5100_Ethernet = WIZ811MJ [package=wiz811mj]  # not connected

nets:
  N1: Arduino_Nano_V3_0.D10, JP1.NSS, JP1.RST
  N2: Arduino_Nano_V3_0.D11/MOSI, JP1.MO
  N3: Arduino_Nano_V3_0.D12/MISO, JP1.MI
  N4: Arduino_Nano_V3_0.VIN, JP1.V+5
  GND: Arduino_Nano_V3_0.GND, JP1.GND
  N5: Arduino_Nano_V3_0.D13/SCK, JP1.SOK

notes:
  relay NC
  WatchDog 2015.10.15
  buzzer
  LED

custom parts:
  Header 5x2: Header 5x2 Standard 10-pin dual row 0.1 header. Commonly used with AVR-ISP. Use with Spark Fun Electronics SKU: PRT-00778
